// Logisim project lab8.circ as structural Verilog: 2 circuits, main circuit main
module main (
  input  x1,
  input  y1,
  input  Cin,
  input  x2,
  input  y2,
  input  [3:0] X,
  input  x3,
  input  y3,
  input  [3:0] Y,
  input  x4,
  input  y4,
  output [4:0] S
);

  wire and_1_out, and_2_out, and_3_out, and_4_out, and_5_out, and_6_out, and_7_out, and_8_out, or_1_out,
       or_2_out, or_3_out, xor_1_out, xor_2_out, xor_3_out, xor_4_out;

  xor xor_1 (xor_1_out, x1, y1);
  and and_1 (and_1_out, x1, y1);
  xor xor_2 (xor_2_out, x2, y2);
  and and_2 (and_2_out, x2, y2);
  xor xor_3 (xor_3_out, x3, y3);
  and and_3 (and_3_out, x3, y3);
  xor xor_4 (xor_4_out, x4, y4);
  and and_4 (and_4_out, x4, y4);
  and and_5 (and_5_out, xor_1_out, Cin);
  and and_6 (and_6_out, xor_2_out, or_1_out);
  and and_7 (and_7_out, xor_3_out, or_2_out);
  and and_8 (and_8_out, xor_4_out, or_3_out);
  xor xor_5 (S[0], xor_1_out, Cin);
  xor xor_6 (S[1], xor_2_out, or_1_out);
  xor xor_7 (S[2], xor_3_out, or_2_out);
  xor xor_8 (S[3], xor_4_out, or_3_out);
  or or_1 (or_1_out, and_5_out, and_1_out);
  or or_2 (or_2_out, and_6_out, and_2_out);
  or or_3 (or_3_out, and_7_out, and_3_out);
  or or_4 (S[4], and_8_out, and_4_out);

  assign {X[2], X[0]} = {X[3], X[1]};
  assign Y[1:0] = {2{Y[2]}};
endmodule

module Full_Adder (
  input  X,
  input  Y,
  input  Z,
  output S,
  output C
);

  wire and_1_out, and_2_out, xor_1_out;

  xor xor_1 (xor_1_out, X, Y);
  and and_1 (and_1_out, X, Y);
  xor xor_2 (S, xor_1_out, Z);
  and and_2 (and_2_out, xor_1_out, Z);
  or or_1 (C, and_2_out, and_1_out);
endmodule
